// Digital circuit 1-bit full adder.dig as structural Verilog
module _1_bit_full_adder (
  input  A,
  input  B,
  input  Carry_in,
  output Sum,
  output Carry_out
);

  wire and_1_out, and_2_out, xor_1_out;

  and and_1 (and_1_out, B, A);
  xor xor_1 (xor_1_out, A, B);
  xor xor_2 (Sum, xor_1_out, Carry_in);
  and and_2 (and_2_out, xor_1_out, Carry_in);
  or or_1 (Carry_out, and_2_out, and_1_out);

  // Notes on the sheet:
  //   Carry_in: i
endmodule
