// Digital circuit 2-bit multiplier.dig as structural Verilog
module _2_bit_multiplier (
  input  A0,
  input  A1,
  input  B0,
  input  B1,
  output P0,
  output P1,
  output P2,
  output P3
);

  wire and_1_out, and_2_out, and_5_out, and_6_out, and_7_out, and_8_out, not_1_out, not_2_out, not_3_out,
       not_4_out;

  not not_1 (not_1_out, A0);
  not not_2 (not_2_out, A1);
  and and_1 (and_1_out, A1, A0, B1);
  and and_2 (and_2_out, A1, B0, B1);
  and and_3 (P0, A0, B0);
  and and_4 (P3, A0, A1, B0, B1);
  not not_3 (not_3_out, B1);
  or or_1 (P2, and_1_out, and_2_out);
  not not_4 (not_4_out, B0);
  and and_5 (and_5_out, A1, not_1_out, B0);
  and and_6 (and_6_out, A1, B0, not_3_out);
  and and_7 (and_7_out, A0, B1, not_2_out);
  and and_8 (and_8_out, A0, B1, not_4_out);
  or or_2 (P1, and_5_out, and_6_out, and_7_out, and_8_out);
endmodule
