// Digital circuit 4-bit chained up adder.dig as structural Verilog
module _4_bit_chained_up_adder (
  input  [3:0] B,
  input  [3:0] A,
  output [3:0] Sum,
  output Overflow_flag
);

  wire _1_bit_full_adder_2_carry_out, _1_bit_full_adder_3_carry_out, _1_bit_full_adder_4_carry_out;

  _1_bit_full_adder _1_bit_full_adder_1 (
    .A(A[3]), .B(B[3]), .Carry_in(_1_bit_full_adder_2_carry_out), .Sum(Sum[3]), .Carry_out(Overflow_flag));
  _1_bit_full_adder _1_bit_full_adder_2 (
    .A(A[2]), .B(B[2]), .Carry_in(_1_bit_full_adder_3_carry_out), .Sum(Sum[2]),
    .Carry_out(_1_bit_full_adder_2_carry_out));
  _1_bit_full_adder _1_bit_full_adder_3 (
    .A(A[1]), .B(B[1]), .Carry_in(_1_bit_full_adder_4_carry_out), .Sum(Sum[1]),
    .Carry_out(_1_bit_full_adder_3_carry_out));
  _1_bit_full_adder _1_bit_full_adder_4 (
    .A(A[0]), .B(B[0]), .Carry_in(1'b0), .Sum(Sum[0]), .Carry_out(_1_bit_full_adder_4_carry_out));
endmodule
